# Fritzing sketch Board (saved by Fritzing 0.9.4)
breadboards: 1

parts:
  J1 = Basic Servo
  J2 = Basic Servo
  J3 = Basic Servo
  J4 = Basic Servo
  Part2 = Adafruit 1.44 inch TFT Breakout [part_number="Adafruit #2088"]
  KEYPAD1 = Membrane Matrix Keypad
  Part3 = Adafruit ItsyBitsy M4 [part_number="Adafruit #3800"]
  J5 = Piezo Speaker
  LED1 = smd LED [color="Red (633nm)" package="0805 [SMD]"]
  LED2 = smd LED [color="Red (633nm)" package="0805 [SMD]"]
  R1 = Resistor [tolerance=±5% resistance=220 package="2010 [SMD]"]

nets:
  GND: J1.gnd, J2.gnd, J3.gnd, J4.gnd, Part2.GND, Part3.GND, J5.pin1, LED1.anode, LED2.anode
  VCC: J1.vcc, J2.vcc, J3.vcc, J4.vcc, Part3.VBUS
  N1: J1.pulse, Part3.D12
  N2: J2.pulse, Part3.D11
  N3: J3.pulse, Part3.D10
  N4: J4.pulse, Part3.D9
  VIN: Part2.VIN, Part3.+3V3
  N5: Part2.SCK, Part3.SCK
  N6: Part2.MISO, Part3.MISO
  N7: Part2.MOSI, Part3.MOSI
  N8: Part2.TFTCS, Part3.D13
  N9: Part2.RESET, Part3.RX_D0
  N10: Part2.TFTDC, Part3.D7
  N11: KEYPAD1.1, Part3.TX_D1
  N12: KEYPAD1.2, Part3.SCL
  N13: KEYPAD1.3, Part3.A5
  N14: KEYPAD1.5, Part3.A2
  N15: KEYPAD1.6, Part3.A3
  N16: KEYPAD1.7, Part3.A4
  N17: Part3.A1, R1.Pin_1
  N18: J5.pin2, LED1.cathode, LED2.cathode, R1.Pin_0

notes:
  Left Foot
  Right Foot
  Left Leg
  Right Leg

custom parts:
  Adafruit 1.44 inch TFT Breakout: This lovely little display breakout is the best way to add a small, colorful and bright display to any project. Since the display uses 4-wire SPI to communicate and has its own pixel-addressable frame buffer, it can be used with every kind of microcontroller. Even a very small one with low memory and few pins available! The 1.44" display has 128x128 color pixels. Unlike the low cost "Nokia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
  Membrane Matrix Keypad: Membrane Matrix 3x4 Keypad
  Adafruit ItsyBitsy M4: What's smaller than a Feather but larger than a Trinket? It's an Adafruit ItsyBitsy M4 Express featuring the Microchip ATSAMD51! Small, powerful, with a ultra fast ATSAMD51 Cortex M4 processor running at 120 MHz - this microcontroller board is perfect when you want something very compact, with a ton of horsepower and a bunch of pins. This Itsy is like a bullet train, with it's 120MHz Cortex M4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
